// Logisim project ALU_dev.circ as structural Verilog: 1 circuit, main circuit main
module main (
  input  \输入数1第1位 ,
  input  \输入数1第2位 ,
  input  \输入数1第3位 ,
  input  \输入数1第4位 ,
  input  \输入数1第5位 ,
  input  \输入数1第6位 ,
  input  \输入数1第7位 ,
  input  \输入数1第8位 ,
  input  \输入数2第1位 ,
  input  \输入数2第2位 ,
  input  \输入数2第3位 ,
  input  \输入数2第4位 ,
  input  \输入数2第5位 ,
  input  \输入数2第6位 ,
  input  \输入数2第7位 ,
  input  \输入数2第8位 ,
  input  \状态码1 ,
  input  \状态码2 ,
  input  \状态码3 ,
  input  \状态码4 ,
  output out_21,
  output out_22,
  output out_23,
  output out_24,
  output out_25,
  output out_26,
  output out_27,
  output out_28
);

  wire [7:0] \_0000加法器_out_17 , \_0001减法器_out_17 , \_0010递增_out_9 , \_0011递减_out_9 , \_0100按位与_输出的第1位 ,
       \_0101按位或_输出的第1位 , \_0110按位异或_输出的第1位 , \_0111按位非_out_9 , \_1000前移1位_out_9 , \_1001后移一位_out_9 ;

  \八位数加法器  \_0000加法器  (
    .\加数1的第1位 (\输入数1第1位 ), .\加数1的第2位 (\输入数1第2位 ), .\加数1的第3位 (\输入数1第3位 ), .\加数1的第4位 (\输入数1第4位 ),
    .\加数1的第5位 (\输入数1第5位 ), .\加数1的第6位 (\输入数1第6位 ), .\加数1的第7位 (\输入数1第7位 ), .\加数1的第8位 (\输入数1第8位 ),
    .\加数2的第1位 (\输入数2第1位 ), .\加数2的第2位 (\输入数2第2位 ), .\加数2的第3位 (\输入数2第3位 ), .\加数2的第4位 (\输入数2第4位 ),
    .\加数2的第5位 (\输入数2第5位 ), .\加数2的第6位 (\输入数2第6位 ), .\加数2的第7位 (\输入数2第7位 ), .\加数2的第8位 (\输入数2第8位 ),
    .out_17(\_0000加法器_out_17 [0]), .out_18(\_0000加法器_out_17 [1]), .out_19(\_0000加法器_out_17 [2]),
    .out_20(\_0000加法器_out_17 [3]), .out_21(\_0000加法器_out_17 [4]), .out_22(\_0000加法器_out_17 [5]),
    .out_23(\_0000加法器_out_17 [6]), .out_24(\_0000加法器_out_17 [7]));
  \八位数减法器  \_0001减法器  (
    .\被减数的第1位 (\输入数1第1位 ), .\被减数的第2位 (\输入数1第2位 ), .\被减数的第3位 (\输入数1第3位 ), .\被减数的第4位 (\输入数1第4位 ),
    .\被减数的第5位 (\输入数1第5位 ), .\被减数的第6位 (\输入数1第6位 ), .\被减数的第7位 (\输入数1第7位 ), .\被减数的第8位 (\输入数1第8位 ),
    .\减数的第1位 (\输入数2第1位 ), .\减数的第2位 (\输入数2第2位 ), .\减数的第3位 (\输入数2第3位 ), .\减数的第4位 (\输入数2第4位 ),
    .\减数的第5位 (\输入数2第5位 ), .\减数的第6位 (\输入数2第6位 ), .\减数的第7位 (\输入数2第7位 ), .\减数的第8位 (\输入数2第8位 ),
    .out_17(\_0001减法器_out_17 [0]), .out_18(\_0001减法器_out_17 [1]), .out_19(\_0001减法器_out_17 [2]),
    .out_20(\_0001减法器_out_17 [3]), .out_21(\_0001减法器_out_17 [4]), .out_22(\_0001减法器_out_17 [5]),
    .out_23(\_0001减法器_out_17 [6]), .out_24(\_0001减法器_out_17 [7]));
  \递增器  \_0010递增  (
    .in_1(\输入数1第1位 ), .in_2(\输入数1第2位 ), .in_3(\输入数1第3位 ), .in_4(\输入数1第4位 ), .in_5(\输入数1第5位 ),
    .in_6(\输入数1第6位 ), .in_7(\输入数1第7位 ), .in_8(\输入数1第8位 ), .out_9(\_0010递增_out_9 [0]),
    .out_10(\_0010递增_out_9 [1]), .out_11(\_0010递增_out_9 [2]), .out_12(\_0010递增_out_9 [3]),
    .out_13(\_0010递增_out_9 [4]), .out_14(\_0010递增_out_9 [5]), .out_15(\_0010递增_out_9 [6]),
    .out_16(\_0010递增_out_9 [7]));
  \递减器  \_0011递减  (
    .in_1(\输入数1第1位 ), .in_2(\输入数1第2位 ), .in_3(\输入数1第3位 ), .in_4(\输入数1第4位 ), .in_5(\输入数1第5位 ),
    .in_6(\输入数1第6位 ), .in_7(\输入数1第7位 ), .in_8(\输入数1第8位 ), .out_9(\_0011递减_out_9 [0]),
    .out_10(\_0011递减_out_9 [1]), .out_11(\_0011递减_out_9 [2]), .out_12(\_0011递减_out_9 [3]),
    .out_13(\_0011递减_out_9 [4]), .out_14(\_0011递减_out_9 [5]), .out_15(\_0011递减_out_9 [6]),
    .out_16(\_0011递减_out_9 [7]));
  \_8位按位与  \_0100按位与  (
    .\第1个数的第1位 (\输入数1第1位 ), .\第1个数的第2位 (\输入数1第2位 ), .\第1个数的第3位 (\输入数1第3位 ), .\第1个数的第4位 (\输入数1第4位 ),
    .\第1个数的第5位 (\输入数1第5位 ), .\第1个数的第6位 (\输入数1第6位 ), .\第1个数的第7位 (\输入数1第7位 ), .\第1个数的第8位 (\输入数1第8位 ),
    .\第2个数的第1位 (\输入数2第1位 ), .\第2个数的第2位 (\输入数2第2位 ), .\第2个数的第3位 (\输入数2第3位 ), .\第2个数的第4位 (\输入数2第4位 ),
    .\第2个数的第5位 (\输入数2第5位 ), .\第2个数的第6位 (\输入数2第6位 ), .\第2个数的第7位 (\输入数2第7位 ), .\第2个数的第8位 (\输入数2第8位 ),
    .\输出的第1位 (\_0100按位与_输出的第1位 [0]), .\输出的第2位 (\_0100按位与_输出的第1位 [1]), .\输出的第3位 (\_0100按位与_输出的第1位 [2]),
    .\输出的第4位 (\_0100按位与_输出的第1位 [3]), .\输出的第5位 (\_0100按位与_输出的第1位 [4]), .\输出的第6位 (\_0100按位与_输出的第1位 [5]),
    .\输出的第7位 (\_0100按位与_输出的第1位 [6]), .\输出的第8位 (\_0100按位与_输出的第1位 [7]));
  \_8位按位或  \_0101按位或  (
    .\第1个数的第1位 (\输入数1第1位 ), .\第1个数的第2位 (\输入数1第2位 ), .\第1个数的第3位 (\输入数1第3位 ), .\第1个数的第4位 (\输入数1第4位 ),
    .\第1个数的第5位 (\输入数1第5位 ), .\第1个数的第6位 (\输入数1第6位 ), .\第1个数的第7位 (\输入数1第7位 ), .\第1个数的第8位 (\输入数1第8位 ),
    .\第2个数的第1位 (\输入数2第1位 ), .\第2个数的第2位 (\输入数2第2位 ), .\第2个数的第3位 (\输入数2第3位 ), .\第2个数的第4位 (\输入数2第4位 ),
    .\第2个数的第5位 (\输入数2第5位 ), .\第2个数的第6位 (\输入数2第6位 ), .\第2个数的第7位 (\输入数2第7位 ), .\第2个数的第8位 (\输入数2第8位 ),
    .\输出的第1位 (\_0101按位或_输出的第1位 [0]), .\输出的第2位 (\_0101按位或_输出的第1位 [1]), .\输出的第3位 (\_0101按位或_输出的第1位 [2]),
    .\输出的第4位 (\_0101按位或_输出的第1位 [3]), .\输出的第5位 (\_0101按位或_输出的第1位 [4]), .\输出的第6位 (\_0101按位或_输出的第1位 [5]),
    .\输出的第7位 (\_0101按位或_输出的第1位 [6]), .\输出的第8位 (\_0101按位或_输出的第1位 [7]));
  \_8位按位异或  \_0110按位异或  (
    .\第1个数的第1位 (\输入数1第1位 ), .\第1个数的第2位 (\输入数1第2位 ), .\第1个数的第3位 (\输入数1第3位 ), .\第1个数的第4位 (\输入数1第4位 ),
    .\第1个数的第5位 (\输入数1第5位 ), .\第1个数的第6位 (\输入数1第6位 ), .\第1个数的第7位 (\输入数1第7位 ), .\第1个数的第8位 (\输入数1第8位 ),
    .\第2个数的第1位 (\输入数2第1位 ), .\第2个数的第2位 (\输入数2第2位 ), .\第2个数的第3位 (\输入数2第3位 ), .\第2个数的第4位 (\输入数2第4位 ),
    .\第2个数的第5位 (\输入数2第5位 ), .\第2个数的第6位 (\输入数2第6位 ), .\第2个数的第7位 (\输入数2第7位 ), .\第2个数的第8位 (\输入数2第8位 ),
    .\输出的第1位 (\_0110按位异或_输出的第1位 [0]), .\输出的第2位 (\_0110按位异或_输出的第1位 [1]), .\输出的第3位 (\_0110按位异或_输出的第1位 [2]),
    .\输出的第4位 (\_0110按位异或_输出的第1位 [3]), .\输出的第5位 (\_0110按位异或_输出的第1位 [4]), .\输出的第6位 (\_0110按位异或_输出的第1位 [5]),
    .\输出的第7位 (\_0110按位异或_输出的第1位 [6]), .\输出的第8位 (\_0110按位异或_输出的第1位 [7]));
  \_8位数按位非  \_0111按位非  (
    .\输入第1位 (\输入数1第1位 ), .\输入第2位 (\输入数1第2位 ), .\输入第3位 (\输入数1第3位 ), .\输入第4位 (\输入数1第4位 ), .\输入第5位 (\输入数1第5位 ),
    .\输入第6位 (\输入数1第6位 ), .\输入第7位 (\输入数1第7位 ), .\输入第8位 (\输入数1第8位 ), .out_9(\_0111按位非_out_9 [0]),
    .out_10(\_0111按位非_out_9 [1]), .out_11(\_0111按位非_out_9 [2]), .out_12(\_0111按位非_out_9 [3]),
    .out_13(\_0111按位非_out_9 [4]), .out_14(\_0111按位非_out_9 [5]), .out_15(\_0111按位非_out_9 [6]),
    .out_16(\_0111按位非_out_9 [7]));
  \前移1位  \_1000前移1位  (
    .in_1(\输入数1第1位 ), .in_2(\输入数1第2位 ), .in_3(\输入数1第3位 ), .in_4(\输入数1第4位 ), .in_5(\输入数1第5位 ),
    .in_6(\输入数1第6位 ), .in_7(\输入数1第7位 ), .in_8(\输入数1第8位 ), .out_9(\_1000前移1位_out_9 [0]),
    .out_10(\_1000前移1位_out_9 [1]), .out_11(\_1000前移1位_out_9 [2]), .out_12(\_1000前移1位_out_9 [3]),
    .out_13(\_1000前移1位_out_9 [4]), .out_14(\_1000前移1位_out_9 [5]), .out_15(\_1000前移1位_out_9 [6]),
    .out_16(\_1000前移1位_out_9 [7]));
  \右移1位  \_1001后移一位  (
    .in_1(\输入数1第1位 ), .in_2(\输入数1第2位 ), .in_3(\输入数1第3位 ), .in_4(\输入数1第4位 ), .in_5(\输入数1第5位 ),
    .in_6(\输入数1第6位 ), .in_7(\输入数1第7位 ), .in_8(\输入数1第8位 ), .out_9(\_1001后移一位_out_9 [0]),
    .out_10(\_1001后移一位_out_9 [1]), .out_11(\_1001后移一位_out_9 [2]), .out_12(\_1001后移一位_out_9 [3]),
    .out_13(\_1001后移一位_out_9 [4]), .out_14(\_1001后移一位_out_9 [5]), .out_15(\_1001后移一位_out_9 [6]),
    .out_16(\_1001后移一位_out_9 [7]));
  \_8位带宽的16选1选择器  \u_8位带宽的16选1选择器_1  (
    .in_1(\_0000加法器_out_17 [0]), .in_2(\_0000加法器_out_17 [1]), .in_3(\_0000加法器_out_17 [2]),
    .in_4(\_0000加法器_out_17 [3]), .in_5(\_0000加法器_out_17 [4]), .in_6(\_0000加法器_out_17 [5]),
    .in_7(\_0000加法器_out_17 [6]), .in_8(\_0000加法器_out_17 [7]), .in_9(\_0001减法器_out_17 [0]),
    .in_10(\_0001减法器_out_17 [1]), .in_11(\_0001减法器_out_17 [2]), .in_12(\_0001减法器_out_17 [3]),
    .in_13(\_0001减法器_out_17 [4]), .in_14(\_0001减法器_out_17 [5]), .in_15(\_0001减法器_out_17 [6]),
    .in_16(\_0001减法器_out_17 [7]), .in_17(\_0010递增_out_9 [0]), .in_18(\_0010递增_out_9 [1]),
    .in_19(\_0010递增_out_9 [2]), .in_20(\_0010递增_out_9 [3]), .in_21(\_0010递增_out_9 [4]),
    .in_22(\_0010递增_out_9 [5]), .in_23(\_0010递增_out_9 [6]), .in_24(\_0010递增_out_9 [7]),
    .in_25(\_0011递减_out_9 [0]), .in_26(\_0011递减_out_9 [1]), .in_27(\_0011递减_out_9 [2]),
    .in_28(\_0011递减_out_9 [3]), .in_29(\_0011递减_out_9 [4]), .in_30(\_0011递减_out_9 [5]),
    .in_31(\_0011递减_out_9 [6]), .in_32(\_0011递减_out_9 [7]), .in_33(\_0100按位与_输出的第1位 [0]),
    .in_34(\_0100按位与_输出的第1位 [1]), .in_35(\_0100按位与_输出的第1位 [2]), .in_36(\_0100按位与_输出的第1位 [3]),
    .in_37(\_0100按位与_输出的第1位 [4]), .in_38(\_0100按位与_输出的第1位 [5]), .in_39(\_0100按位与_输出的第1位 [6]),
    .in_40(\_0100按位与_输出的第1位 [7]), .in_41(\_0101按位或_输出的第1位 [0]), .in_42(\_0101按位或_输出的第1位 [1]),
    .in_43(\_0101按位或_输出的第1位 [2]), .in_44(\_0101按位或_输出的第1位 [3]), .in_45(\_0101按位或_输出的第1位 [4]),
    .in_46(\_0101按位或_输出的第1位 [5]), .in_47(\_0101按位或_输出的第1位 [6]), .in_48(\_0101按位或_输出的第1位 [7]),
    .in_49(\_0110按位异或_输出的第1位 [0]), .in_50(\_0110按位异或_输出的第1位 [1]), .in_51(\_0110按位异或_输出的第1位 [2]),
    .in_52(\_0110按位异或_输出的第1位 [3]), .in_53(\_0110按位异或_输出的第1位 [4]), .in_54(\_0110按位异或_输出的第1位 [5]),
    .in_55(\_0110按位异或_输出的第1位 [6]), .in_56(\_0110按位异或_输出的第1位 [7]), .in_57(\_0111按位非_out_9 [0]),
    .in_58(\_0111按位非_out_9 [1]), .in_59(\_0111按位非_out_9 [2]), .in_60(\_0111按位非_out_9 [3]),
    .in_61(\_0111按位非_out_9 [4]), .in_62(\_0111按位非_out_9 [5]), .in_63(\_0111按位非_out_9 [6]),
    .in_64(\_0111按位非_out_9 [7]), .in_65(\_1000前移1位_out_9 [0]), .in_66(\_1000前移1位_out_9 [1]),
    .in_67(\_1000前移1位_out_9 [2]), .in_68(\_1000前移1位_out_9 [3]), .in_69(\_1000前移1位_out_9 [4]),
    .in_70(\_1000前移1位_out_9 [5]), .in_71(\_1000前移1位_out_9 [6]), .in_72(\_1000前移1位_out_9 [7]),
    .in_73(\_1001后移一位_out_9 [0]), .in_74(\_1001后移一位_out_9 [1]), .in_75(\_1001后移一位_out_9 [2]),
    .in_76(\_1001后移一位_out_9 [3]), .in_77(\_1001后移一位_out_9 [4]), .in_78(\_1001后移一位_out_9 [5]),
    .in_79(\_1001后移一位_out_9 [6]), .in_80(\_1001后移一位_out_9 [7]), .in_81(\输入数1第1位 ), .in_82(\输入数1第2位 ),
    .in_83(\输入数1第3位 ), .in_84(\输入数1第4位 ), .in_85(\输入数1第5位 ), .in_86(\输入数1第6位 ), .in_87(\输入数1第7位 ),
    .in_88(\输入数1第8位 ), .in_89(\输入数1第1位 ), .in_90(\输入数1第2位 ), .in_91(\输入数1第3位 ), .in_92(\输入数1第4位 ),
    .in_93(\输入数1第5位 ), .in_94(\输入数1第6位 ), .in_95(\输入数1第7位 ), .in_96(\输入数1第8位 ), .in_97(\输入数1第1位 ),
    .in_98(\输入数1第2位 ), .in_99(\输入数1第3位 ), .in_100(\输入数1第4位 ), .in_101(\输入数1第5位 ), .in_102(\输入数1第6位 ),
    .in_103(\输入数1第7位 ), .in_104(\输入数1第8位 ), .in_105(\输入数1第1位 ), .in_106(\输入数1第2位 ), .in_107(\输入数1第3位 ),
    .in_108(\输入数1第4位 ), .in_109(\输入数1第5位 ), .in_110(\输入数1第6位 ), .in_111(\输入数1第7位 ), .in_112(\输入数1第8位 ),
    .in_113(\输入数1第1位 ), .in_114(\输入数1第2位 ), .in_115(\输入数1第3位 ), .in_116(\输入数1第4位 ), .in_117(\输入数1第5位 ),
    .in_118(\输入数1第6位 ), .in_119(\输入数1第7位 ), .in_120(\输入数1第8位 ), .in_121(\输入数1第1位 ), .in_122(\输入数1第2位 ),
    .in_123(\输入数1第3位 ), .in_124(\输入数1第4位 ), .in_125(\输入数1第5位 ), .in_126(\输入数1第6位 ), .in_127(\输入数1第7位 ),
    .in_128(\输入数1第8位 ), .\控制码1 (\状态码1 ), .\控制码2 (\状态码2 ), .\控制码3 (\状态码3 ), .\控制码4 (\状态码4 ), .out_133(out_21),
    .out_134(out_22), .out_135(out_23), .out_136(out_24), .out_137(out_25), .out_138(out_26),
    .out_139(out_27), .out_140(out_28));
endmodule
